# Fritzing sketch LED2 (saved by Fritzing 0.9.3b)
breadboards: 1

parts:
  LED1 = LED - 5mm [color="Red (633nm)" package="5 mm [THT]"]
  パーツ1 = Arduino Uno (Rev3)
  R1 = Resistor [tolerance=±5% resistance=1k package=THT]

nets:
  N1: LED1.cathode, パーツ1.GND
  N2: LED1.anode, R1.Pin_0
  N3: パーツ1.D7, R1.Pin_1
