# Fritzing sketch Motor1 (saved by Fritzing 0.9.3b)
breadboards: 1

parts:
  パーツ1 = Arduino Uno (Rev3)
  R4 = Resistor [tolerance=±5% resistance=100 package=THT]
  R5 = Resistor [tolerance=±5% resistance=100 package=THT]
  R6 = Resistor [tolerance=±5% resistance=100 package=THT]
  R7 = Resistor [tolerance=±5% resistance=100 package=THT]
  M1 = DC Motor
  VCC1 = Battery
  U1 = IC, SIP package, 10 pins [chip_label=MP4207]

nets:
  N1: パーツ1.D8, R4.Pin_0
  N2: パーツ1.D9_PWM, R6.Pin_0
  N3: パーツ1.GND, R5.Pin_0, R7.Pin_0, VCC1.-, U1.pin1
  N4: R4.Pin_1, U1.pin8
  N5: R5.Pin_1, U1.pin6
  N6: R6.Pin_1, U1.pin4
  N7: R7.Pin_1, U1.pin2
  N8: M1.pin_1, U1.pin5, U1.pin9
  N9: M1.pin_2, U1.pin3, U1.pin7
  N10: VCC1.+, U1.pin10
