# Fritzing sketch Motor2 (saved by Fritzing 0.9.3b)
breadboards: 1

parts:
  パーツ1 = Arduino Uno (Rev3)
  M1 = DC Motor
  VCC1 = Battery
  U1 = IC, SIP package, 10 pins [chip_label=MP4207]

nets:
  N1: パーツ1.D10_PWM/SS, U1.pin6
  N2: パーツ1.D11_PWM/MOSI, U1.pin4
  N3: パーツ1.D12/MISO, U1.pin8
  N4: パーツ1.D13/SCK, U1.pin2
  N5: パーツ1.GND, VCC1.-, U1.pin1
  N6: M1.pin_1, U1.pin5, U1.pin9
  N7: M1.pin_2, U1.pin3, U1.pin7
  N8: VCC1.+, U1.pin10
